# Fritzing sketch trafficlights (saved by Fritzing 0.9.1b)
breadboards: 1

parts:
  S1 = Momentary Switch [package=ksa_sealed_tac_switch]
  Raspberry_Pi1 = Raspberry Pi B+
  LED1 = smd LED [color="Red (633nm)" package="1206 [SMD]"]
  LED2 = LED - 3mm [color="Yellow (595nm)" package="3 mm [THT]"]
  LED3 = LED - 3mm [color="Green (570nm)" package="3 mm [THT]"]
  R1 = Resistor [tolerance=±5% resistance=220 package=THT]
  R2 = Resistor [tolerance=±5% resistance=220 package=THT]
  R3 = Resistor [tolerance=±5% resistance=220 package=THT]
  J1 = Piezo Speaker

nets:
  N1: S1.1, Raspberry_Pi1.GND, LED1.cathode, LED2.cathode, LED3.cathode, J1.pin1
  N2: S1.3, Raspberry_Pi1.GPIO23
  N3: Raspberry_Pi1.GPIO25, J1.pin2
  N4: Raspberry_Pi1.GPIO18, R3.Pin_0
  N5: Raspberry_Pi1.GPIO15, R2.Pin_0
  N6: Raspberry_Pi1.GPIO14, R1.Pin_0
  N7: LED1.anode, R1.Pin_1
  N8: LED2.anode, R2.Pin_1
  N9: LED3.anode, R3.Pin_1
